// Logisim project LAB2.circ as structural Verilog: 1 circuit, main circuit main
module main (
  input  A,
  input  B,
  input  A_2,
  input  B_2,
  input  C_prime,
  input  A_3,
  input  B_3,
  input  C,
  output AB_prime_BC_prime_AC_prime,
  output out_10
);

  wire and_1_out, and_2_out, and_3_out, and_4_out, and_5_out, and_6_out, and_7_out, and_8_out, and_9_out,
       and_10_out, and_11_out, and_12_out, and_13_out, not_1_out, not_2_out, not_3_out, not_4_out, not_5_out,
       not_6_out, not_7_out, or_1_out, or_2_out, or_3_out, or_5_out, or_6_out;

  not not_1 (not_1_out, B);
  not not_2 (not_2_out, B_2);
  not not_3 (not_3_out, C_prime);
  not not_4 (not_4_out, A);
  not not_5 (not_5_out, A_3);
  not not_6 (not_6_out, B_3);
  not not_7 (not_7_out, C);
  and and_1 (and_1_out, A, not_1_out);
  and and_2 (and_2_out, not_4_out, not_1_out);
  and and_3 (and_3_out, not_4_out, B);
  and and_4 (and_4_out, A_2, not_2_out);
  and and_5 (and_5_out, B_2, not_3_out);
  and and_6 (and_6_out, A_2, not_3_out);
  and and_7 (and_7_out, not_5_out, not_6_out);
  and and_8 (and_8_out, A_3, B_3);
  and and_9 (and_9_out, B_3, not_5_out);
  or or_1 (or_1_out, and_1_out, and_2_out);
  or or_2 (or_2_out, and_4_out, and_5_out);
  or or_3 (or_3_out, or_1_out, and_3_out);
  or or_4 (AB_prime_BC_prime_AC_prime, or_2_out, and_6_out);
  and and_10 (and_10_out, and_7_out, C);
  and and_11 (and_11_out, and_8_out, not_7_out);
  and and_12 (and_12_out, and_9_out, not_7_out);
  and and_13 (and_13_out, not_7_out, and_7_out);
  LED led_1 (.in(or_3_out));
  or or_5 (or_5_out, and_10_out, and_11_out);
  or or_6 (or_6_out, and_12_out, and_13_out);
  or or_7 (out_10, or_5_out, or_6_out);

  // Notes on the sheet:
  //   3.
  //   2.
  //   C
  //   A'
  //   B'
  //   B'
  //   1.
  //   A'
  //   A
  //   B
  //   B
  //   A'
  //   AB'
  //   A'B'
  //   AB'
  //   BC'
  //   B'
  //   B
  //   AB'+BC'
  //   AB'+A'B'
  //   A'B
  //   AC'
  //   A'B'
  //   C'
  //   C
  //   AB
  //   C'
  //   A'B
  //   C'
  //   A'B'
  //   AB'+A'B'+A'B
  //   A'B'C
  //   ABC'
  //   A'BC'
  //   A'B'C'
  //   A'B'C+ABC'
  //   A'BC'+A'B'C'
  //   A'B'C+ABC'+A'BC'+A'B'C'
endmodule
