// Logisim project LAB5_Q2.circ as structural Verilog: 2 circuits, main circuit main
module main (
  input  [3:0] in_1,
  input  [3:0] in_2,
  output B0,
  output B1,
  output B2,
  output B3,
  output out_7,
  output C
);

  wire and_1_out, and_2_out, fulladder_1_c;
  wire [3:0] fulladder_1_s0;

  fulladder fulladder_1 (
    .X(in_1), .Z(1'b0), .Y(in_2), .S0(fulladder_1_s0[0]), .S1(fulladder_1_s0[1]), .S2(fulladder_1_s0[2]),
    .S3(fulladder_1_s0[3]), .C(fulladder_1_c));
  and and_1 (and_1_out, fulladder_1_s0[0], fulladder_1_s0[1]);
  and and_2 (and_2_out, fulladder_1_s0[2], fulladder_1_s0[3]);
  or or_1 (C, and_1_out, and_2_out, fulladder_1_c);
  fulladder fulladder_2 (
    .X({1'b0, {2{C}}, 1'b0}), .Z(fulladder_1_c), .Y(fulladder_1_s0), .S0(B0), .S1(B1), .S2(B2), .S3(B3),
    .C(out_7));
endmodule

module fulladder (
  input  [3:0] X,
  input  Z,
  input  [3:0] Y,
  output S0,
  output S1,
  output S2,
  output S3,
  output C
);

  wire and_1_out, and_2_out, and_3_out, and_4_out, and_5_out, and_6_out, and_7_out, and_8_out, and_9_out,
       and_10_out, and_11_out, and_12_out, or_1_out, or_2_out, or_3_out, or_4_out, or_5_out, or_6_out,
       or_7_out, xor_1_out, xor_3_out, xor_5_out, xor_7_out;

  xor xor_1 (xor_1_out, X[0], Y[0]);
  and and_1 (and_1_out, X[0], Y[0]);
  and and_2 (and_2_out, Y[0], Z);
  and and_3 (and_3_out, X[0], Z);
  xor xor_2 (S0, xor_1_out, Z);
  or or_1 (or_1_out, and_1_out, and_2_out);
  or or_2 (or_2_out, or_1_out, and_3_out);
  xor xor_3 (xor_3_out, X[1], Y[1]);
  and and_4 (and_4_out, X[1], Y[1]);
  and and_5 (and_5_out, Y[1], or_2_out);
  and and_6 (and_6_out, X[1], or_2_out);
  or or_3 (or_3_out, and_4_out, and_5_out);
  xor xor_4 (S1, xor_3_out, or_2_out);
  or or_4 (or_4_out, or_3_out, and_6_out);
  xor xor_5 (xor_5_out, X[2], Y[2]);
  and and_7 (and_7_out, X[2], Y[2]);
  and and_8 (and_8_out, Y[2], or_4_out);
  and and_9 (and_9_out, X[2], or_4_out);
  xor xor_6 (S2, xor_5_out, or_4_out);
  or or_5 (or_5_out, and_7_out, and_8_out);
  or or_6 (or_6_out, or_5_out, and_9_out);
  xor xor_7 (xor_7_out, X[3], Y[3]);
  and and_10 (and_10_out, X[3], Y[3]);
  and and_11 (and_11_out, Y[3], or_6_out);
  and and_12 (and_12_out, X[3], or_6_out);
  xor xor_8 (S3, xor_7_out, or_6_out);
  or or_7 (or_7_out, and_10_out, and_11_out);
  or or_8 (C, or_7_out, and_12_out);

  // Notes on the sheet:
  //   X
  //   Y
  //   S
  //   C
  //   X
  //   Y
  //   Z
  //   S
  //   C
  //   X
  //   Y
  //   Z
  //   S
  //   C
  //   X
  //   Y
  //   Z
  //   S
  //   C
endmodule
