// Logisim project LAB_6_LOOK_AHEAD_CARRY.circ as structural Verilog: 1 circuit, main circuit main
module main (
  input  C0,
  input  [3:0] X,
  input  [3:0] Y,
  output out_4,
  output out_5,
  output out_6,
  output out_7,
  output out_8
);

  wire and_1_out, and_2_out, and_3_out, and_4_out, and_5_out, and_6_out, and_7_out, and_8_out, and_9_out,
       and_10_out, C1_out, C2_out, C3_out, G0_out, G1_out, G2_out, G3_out, P0_out, P1_out, P2_out, P3_out;

  xor P1 (P1_out, X[1], Y[1]);
  and G1 (G1_out, X[1], Y[1]);
  xor P2 (P2_out, X[2], Y[2]);
  and G2 (G2_out, X[2], Y[2]);
  and G3 (G3_out, X[3], Y[3]);
  xor P3 (P3_out, X[3], Y[3]);
  xor P0 (P0_out, X[0], Y[0]);
  and G0 (G0_out, X[0], Y[0]);
  and and_1 (and_1_out, C0, P0_out);
  and and_2 (and_2_out, C0, P0_out, P1_out);
  and and_3 (and_3_out, G0_out, P1_out);
  and and_4 (and_4_out, P0_out, P1_out, P2_out, C0);
  and and_5 (and_5_out, P2_out, P1_out, G0_out);
  and and_6 (and_6_out, P2_out, G1_out);
  and and_7 (and_7_out, C0, P0_out, P1_out, P2_out, P3_out);
  and and_8 (and_8_out, G0_out, P1_out, P2_out, P3_out);
  and and_9 (and_9_out, G1_out, P2_out, P3_out);
  and and_10 (and_10_out, G2_out, P3_out);
  or C1 (C1_out, and_1_out, G0_out);
  or C2 (C2_out, and_2_out, and_3_out, G1_out);
  or C3 (C3_out, and_4_out, and_5_out, and_6_out, G2_out);
  or C4 (out_8, and_7_out, and_8_out, and_9_out, and_10_out, G3_out);
  xor S0 (out_4, C0, P0_out);
  xor S1 (out_5, C1_out, P1_out);
  xor S2 (out_6, C2_out, P2_out);
  xor S3 (out_7, C3_out, P3_out);
endmodule
