// Logisim project Lab3.circ as structural Verilog: 1 circuit, main circuit main
module main (
  input  [3:0] in_1,
  input  Z,
  input  [3:0] Y
);

  wire and_1_out, and_2_out, and_3_out, and_4_out, and_5_out, and_6_out, and_7_out, and_8_out, and_9_out,
       and_10_out, and_11_out, and_12_out, or_1_out, or_2_out, or_3_out, or_4_out, or_5_out, or_6_out,
       or_7_out, xor_1_out, xor_3_out, xor_5_out, xor_7_out;
  wire [0:0] or_8_out;
  wire [3:0] xor_2_out;

  xor xor_1 (xor_1_out, in_1[0], Y[0]);
  and and_1 (and_1_out, in_1[0], Y[0]);
  and and_2 (and_2_out, Y[0], Z);
  and and_3 (and_3_out, in_1[0], Z);
  xor xor_2 (xor_2_out[0], xor_1_out, Z);
  or or_1 (or_1_out, and_1_out, and_2_out);
  or or_2 (or_2_out, or_1_out, and_3_out);
  xor xor_3 (xor_3_out, in_1[1], Y[1]);
  and and_4 (and_4_out, in_1[1], Y[1]);
  and and_5 (and_5_out, Y[1], or_2_out);
  and and_6 (and_6_out, in_1[1], or_2_out);
  or or_3 (or_3_out, and_4_out, and_5_out);
  xor xor_4 (xor_2_out[1], xor_3_out, or_2_out);
  or or_4 (or_4_out, or_3_out, and_6_out);
  xor xor_5 (xor_5_out, in_1[2], Y[2]);
  and and_7 (and_7_out, in_1[2], Y[2]);
  and and_8 (and_8_out, Y[2], or_4_out);
  and and_9 (and_9_out, in_1[2], or_4_out);
  xor xor_6 (xor_2_out[2], xor_5_out, or_4_out);
  or or_5 (or_5_out, and_7_out, and_8_out);
  or or_6 (or_6_out, or_5_out, and_9_out);
  xor xor_7 (xor_7_out, in_1[3], Y[3]);
  and and_10 (and_10_out, in_1[3], Y[3]);
  and and_11 (and_11_out, Y[3], or_6_out);
  and and_12 (and_12_out, in_1[3], or_6_out);
  xor xor_8 (xor_2_out[3], xor_7_out, or_6_out);
  or or_7 (or_7_out, and_10_out, and_11_out);
  or or_8 (or_8_out[0], or_7_out, and_12_out);
  Hex_Digit_Display hex_digit_display_1 (.value({3'b000, or_8_out[0]}));  // open: dp
  Hex_Digit_Display hex_digit_display_2 (.value(xor_2_out));  // open: dp

  // Notes on the sheet:
  //   X
  //   X
  //   Y
  //   S
  //   C
  //   X
  //   Y
  //   Z
  //   S
  //   C
  //   X
  //   Y
  //   Z
  //   S
  //   C
  //   X
  //   Y
  //   Z
  //   S
  //   C
  //   C
  //   S
endmodule
