// Logisim project lab4_q2.circ as structural Verilog: 3 circuits, main circuit main
module main (
  input  in_1,
  input  in_2,
  input  in_3,
  input  in_4,
  input  in_5,
  input  in_6,
  input  in_7,
  input  in_8
);

  wire compare_1_l1, compare_1_l2, compare_1_l3, encode_1_x, encode_1_y, encode_2_x, encode_2_y, or_1_out,
       or_2_out;

  encode encode_1 (.D0(in_1), .D1(in_2), .D2(in_3), .D3(in_4), .Y(encode_1_y), .X(encode_1_x));
  encode encode_2 (.D0(in_5), .D1(in_6), .D2(in_7), .D3(in_8), .Y(encode_2_y), .X(encode_2_x));
  compare compare_1 (
    .A1(encode_1_x), .B1(encode_2_x), .A0(encode_1_y), .B0(encode_2_y), .L1(compare_1_l1), .L2(compare_1_l2),
    .L3(compare_1_l3));
  or or_1 (or_1_out, compare_1_l1, compare_1_l3);
  LED led_1 (.in(or_1_out));
  or or_2 (or_2_out, compare_1_l2, compare_1_l3);
  LED led_2 (.in(or_2_out));
  LED led_3 (.in(compare_1_l3));

  // Notes on the sheet:
  //   A>B
  //   A<B
  //   A=B
endmodule

module encode (
  input  D0,
  input  D1,
  input  D2,
  input  D3,
  output Y,
  output X
);

  or or_1 (Y, D1, D3);
  or or_2 (X, D2, D3);
endmodule

module compare (
  input  A1,
  input  B1,
  input  A0,
  input  B0,
  output L1,
  output L2,
  output L3
);

  wire and_1_out, and_2_out, and_3_out, and_4_out, and_6_out, and_7_out, nor_1_out, nor_2_out, not_1_out,
       not_2_out, not_3_out, not_4_out, not_5_out, not_6_out;

  not not_1 (not_1_out, A1);
  not not_2 (not_2_out, B1);
  not not_3 (not_3_out, A0);
  not not_4 (not_4_out, B0);
  and and_1 (and_1_out, A1, not_2_out);
  and and_2 (and_2_out, B1, not_1_out);
  and and_3 (and_3_out, A0, not_4_out);
  and and_4 (and_4_out, not_3_out, B0);
  nor nor_1 (nor_1_out, and_1_out, and_2_out);
  nor nor_2 (nor_2_out, and_3_out, and_4_out);
  and and_5 (L3, nor_1_out, nor_2_out);
  not not_5 (not_5_out, L3);
  not not_6 (not_6_out, L3);
  and and_6 (and_6_out, not_5_out, and_3_out);
  and and_7 (and_7_out, not_6_out, and_4_out);
  or or_1 (L1, and_1_out, and_6_out);
  or or_2 (L2, and_2_out, and_7_out);
endmodule
