// Logisim project lab5.circ as structural Verilog: 2 circuits, main circuit main
module main (
  input  B3,
  input  B2,
  input  B1,
  input  B0
);

  wire [2:0] xor_3_out;

  xor xor_1 (xor_3_out[2], B3, B2);
  xor xor_2 (xor_3_out[1], B2, B1);
  xor xor_3 (xor_3_out[0], B1, B0);
  Hex_Digit_Display hex_digit_display_1 (.value({B3, xor_3_out}));  // open: dp
endmodule

module graytobinary (
  input  G3,
  input  G2,
  input  G1,
  input  G0
);

  wire [2:0] xor_3_out;

  xor xor_1 (xor_3_out[2], G3, G2);
  xor xor_2 (xor_3_out[1], xor_3_out[2], G1);
  xor xor_3 (xor_3_out[0], xor_3_out[1], G0);
  Hex_Digit_Display hex_digit_display_1 (.value({G3, xor_3_out}));  // open: dp
endmodule
